# Fritzing sketch standing-desk (saved by Fritzing 0.9.6b)

parts:
  S1 = Round Pushbutton
  S2 = Round Pushbutton
  HC-SR04_Sensor_1 = HC-SR04 Ultrasonic Distance Sensor
  Part3 = Motor Driver 1A Dual TB6612FNG
  M1 = DC Motor
  Power_plug1 = Power plug
  R1 = Resistor [tolerance=±1% resistance=10k package="2512 [SMD]"]
  R2 = Resistor [tolerance=±1% resistance=10k package="2512 [SMD]"]
  Part2 = Arduino Uno (Rev3) - ICSP

nets:
  VCC: S1.leg0, S2.leg0, HC-SR04_Sensor_1.VCC, Part2.5V
  N1: S1.leg1, R2.Pin_0, Part2.ICSP_MISO, Part2.D12/MISO
  N2: S2.leg1, R1.Pin_0, Part2.D13/SCK
  N3: HC-SR04_Sensor_1.TRIG, Part2.D5_PWM
  N4: HC-SR04_Sensor_1.ECHO, Part2.D7
  GND: HC-SR04_Sensor_1.GND, Part3.GND, Power_plug1.GND, R1.Pin_1, R2.Pin_1, Part2.GND
  N5: Part3.A02, M1.pin_1
  N6: Part3.A01, M1.pin_2
  VCC_2: Part3.VM, Power_plug1.VCC, Part2.VIN
  N7: Part3.PWMA, Part2.D6_PWM
  N8: Part3.AIN2, Part2.D4
  N9: Part3.AIN1, Part2.D3_PWM
  N10: Part3.STBY, Part2.D10_PWM/SS

notes:
  Raise button
  Lower button
  12V
  VM
  AO1
  AO2
  VCC
  GND
  STBY
  PWMA
  AI2
  AI1
